# Fritzing sketch GATHRA (saved by Fritzing 1.0.7)

parts:
  Part1 = HY-SRF05 Ultrasonic Rangefinder
  DHT1 = DHT22 Humidity and Temperature Sensor
  A2 = CN3065 Mini Solar Charger Module
  M1 = Osoyoo SX1278-ra-02
  6V_Solar_Panel = Small 6V Solar Panel [mn=? mpn=? part_number=?]
  18650_Battery = Battery
  A3 = mini boost module
  Part3 = I2C level shifter bidirectional
  A1 = Esp32-c3 super mini
  R2 = Resistor [tolerance=±5% power=0.25W resistance=5k package=THT]
  R1 = Resistor [tolerance=±5% power=0.25W resistance=10k package=THT]
  S1 = Pushbutton [package="[THT]"]

nets:
  +5V: Part1.Vcc, DHT1.VDD, A3.Pin_4, Part3.HV, A1.Pin_16
  N1: Part1.Trig, Part3.HV2
  N2: Part1.Echo, Part3.HV1
  GND: Part1.GND, DHT1.GND, M1.GND, A3.Pin_3, Part3.GND, A1.Pin_15, S1.Pin_1, S1.Pin_2
  N3: DHT1.DATA, Part3.HV3
  N4: A2.Pin_1, A2.Pin_3, 6V_Solar_Panel.+
  N5: A2.Pin_2, A2.Pin_4, A2.Pin_5, A2.Pin_8, A2.Pin_10, 6V_Solar_Panel.-, 18650_Battery.-, A3.Pin_1, R2.Pin_1
  N6: A2.Pin_6, A2.Pin_7, A2.Pin_9, 18650_Battery.+, A3.Pin_2, R1.Pin_0
  +3.3V: M1.3.3V, Part3.LV, A1.Pin_14
  N7: M1.RST, A1.Pin_10
  N8: M1.DIO0, A1.Pin_12
  N9: M1.SCK, A1.Pin_13
  N10: M1.MISO, A1.Pin_1
  N11: M1.MOSI, A1.Pin_2
  N12: M1.NSS, A1.Pin_3
  N13: Part3.LV3, A1.Pin_6
  N14: Part3.LV2, A1.Pin_7
  N15: Part3.LV1, A1.Pin_8
  N16: A1.Pin_9, R2.Pin_0, R1.Pin_1
  N17: A1.Pin_11, S1.Pin_3, S1.Pin_4

notes:
  Voltage Divider
  HY-SRF05

custom parts:
  CN3065 Mini Solar Charger Module: Fc-51 Infrared Obstacle Avoidance Proximity Sensor module. IR transmitter led, receiver LED, lm393 compaitor and a pot. 3.3 V to 5V power.
  Osoyoo SX1278-ra-02: Osoyoo Long Distance wireless transceiver Uart LoRa Module.
  Battery: Your standard 2x 18650 battery pack (7.4 Volts)
  mini boost module: mini boost module.
  Esp32-c3 super mini: ESP32-C3 Development Board ESP32 SuperMini Development Board ESP32 Development Board WiFi Bluetooth.
